# Fritzing sketch Bluetooth (saved by Fritzing 0.9.3b)
breadboards: 1

parts:
  Parça1 = HC-05 [part_number=HC-05 package="breakout board"]
  R1 = Resistor [tolerance=±5% resistance=10k package=THT]
  R2 = Resistor [tolerance=±5% resistance=10k package=THT]
  R3 = Resistor [tolerance=±5% resistance=10k package=THT]
  Parça2 = Arduino Uno (Rev3)

nets:
  VCC: Parça1.VCC, Parça2.5V
  GND: Parça1.GND, R1.Pin_0, Parça2.GND
  N1: Parça1.TXD, Parça2.D7
  N2: Parça1.RXD, R2.Pin_1, R3.Pin_1
  N3: R1.Pin_1, R2.Pin_0
  N4: R3.Pin_0, Parça2.D8

custom parts:
  HC-05: A commonly available HC-05 Bluetooth breakout board.
