# Fritzing sketch Step-motor-hız-speed (saved by Fritzing 0.9.3b)
breadboards: 1

parts:
  Parça2 = Arduino Uno (Rev3)
  SM2 = 28BYJ-48 Stepper Motor [part_number=28BYJ-48]
  Driver2 = 28BYJ-48 Driver Module [part_number=ULN2003 package=THT]
  R1 = Rotary Potentiometer (Small) [maximum_resistance=100kΩ package=THT]

nets:
  N1: Parça2.A0, R1.wiper
  N2: Parça2.D8, Driver2.IN4
  N3: Parça2.D9_PWM, Driver2.IN3
  N4: Parça2.D10_PWM/SS, Driver2.IN2
  N5: Parça2.D11_PWM/MOSI, Driver2.IN1
  N6: Parça2.5V, Driver2.Vmotor, R1.leg2
  N7: SM2.blue-pin, Driver2.blue-pin
  N8: SM2.pink-pin, Driver2.pink-pin
  N9: SM2.yellow-pin, Driver2.yellow-pin
  N10: SM2.orange-pin, Driver2.orange-pin
  N11: SM2.red-pin, Driver2.red-pin
  N12: Driver2.GND, R1.leg1

custom parts:
  28BYJ-48 Stepper Motor: Unipolar Stepper Motor 28BYJ-48 Top coil - pink & orange Bottom coil - blue & yellow Common rail - red Connector pins: blue - pink - yellow - orange - red
  28BYJ-48 Driver Module: ULN2003 Driver Module for the 28BYJ-48 Unipolar Stepper Motor LED A - Blue wire - Bottom coil left LED B - Pink wire - Top coil left LED C - Yellow wire - Bottom coil right LED D - Orange wire - Top coil right Common rail - red Connector pins: blue - pink - yellow - orange - red Control pins - IN1 to IN4 Power pins - GND & Vmotor (5-12V) On/Off jumper (if removed, power to motor is cut).
