# Fritzing sketch analog_giris (saved by Fritzing 0.9.3b)
breadboards: 1

parts:
  Parça1 = Arduino Uno (Rev3)
  R1 = Resistor [tolerance=±5% resistance=220 package=THT]
  R2 = Resistor [tolerance=±5% resistance=220 package=THT]

nets:
  N1: Parça1.A0, R1.Pin_0, R2.Pin_1
  N2: Parça1.GND, R1.Pin_1
  N3: Parça1.5V, R2.Pin_0
