# Fritzing sketch araba (saved by Fritzing 0.9.3b)
breadboards: 1

parts:
  L298N1 = L298N DC motor driver
  M1 = DC Motor
  M2 = DC Motor
  Parça1 = Arduino Uno (Rev3)
  hc-sr1 = hc-sr04
  VCC1 = Battery  # not connected
  VCC2 = Battery
  S1 = Toggle Switch [package=THT]

nets:
  N1: L298N1.OUT1, M1.pin_2
  N2: L298N1.OUT2, M1.pin_1
  N3: L298N1.OUT3, M2.pin_2
  N4: L298N1.OUT4, M2.pin_1
  12V: L298N1.12V, Parça1.VIN, S1.L2
  GND: L298N1.GND, Parça1.GND, hc-sr1.GND, VCC2.-
  N5: L298N1.ENA, Parça1.D10_PWM/SS
  N6: L298N1.ENB, Parça1.D3_PWM
  N7: L298N1.IN1, Parça1.D7
  N8: L298N1.IN2, Parça1.D6_PWM
  N9: L298N1.IN3, Parça1.D5_PWM
  N10: L298N1.IN4, Parça1.D4
  N11: Parça1.D12/MISO, hc-sr1.Echo
  N12: Parça1.D13/SCK, hc-sr1.Trig
  5V: Parça1.5V, hc-sr1.VCC

custom parts:
  L298N DC motor driver: 2x DC motor driver with 78M05 positive voltage regulator (7..35 V) L298N: max 46 V, 2 A Set 5 V Enable jumper to enable 5 V regultor (needed for the L298N) and +5 V output at screw terminal or supply external +5 V at screw terminal Set ENA and/or ENB to +5 V to enable motor permanently or supply ENA and/or ENB with PWM signal IN1 and IN2 set rotation directory for motor A (OUT1/OUT2) IN2 and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
