# Fritzing sketch button2_sintal (saved by Fritzing 0.9.3b)
breadboards: 1

parts:
  Parça1 = Arduino Uno (Rev3)
  LED1 = LED - 5mm [color="Red (633nm)" package="5 mm [THT]"]
  R1 = Resistor [tolerance=±5% resistance=220 package=THT]
  S1 = Pushbutton [package="[THT]"]
  R2 = Resistor [tolerance=±5% resistance=220 package=THT]
  S2 = Pushbutton [package="[THT]"]
  R3 = Resistor [tolerance=±5% resistance=220 package=THT]

nets:
  N1: Parça1.D9_PWM, LED1.cathode
  N2: Parça1.D10_PWM/SS, S1.Pin_1, S1.Pin_2, R2.Pin_1
  N3: Parça1.D11_PWM/MOSI, S2.Pin_1, S2.Pin_2, R3.Pin_1
  N4: Parça1.5V, S1.Pin_3, S1.Pin_4, S2.Pin_3, S2.Pin_4
  N5: Parça1.GND, R1.Pin_0, R2.Pin_0, R3.Pin_0
  N6: LED1.anode, R1.Pin_1
