# Fritzing sketch buzzer_led (saved by Fritzing 0.9.3b)
breadboards: 1

parts:
  Parça1 = Arduino Uno (Rev3)
  J1 = Piezo Speaker
  LED1 = LED - 5mm [color="Red (633nm)" package="5 mm [THT]"]
  R1 = Resistor [tolerance=±5% resistance=220 package=THT]
  R2 = Rotary Potentiometer (Small) [maximum_resistance=100kΩ package=THT]
  R3 = Resistor [tolerance=±5% resistance=220 package=THT]

nets:
  N1: Parça1.A0, R2.wiper
  N2: Parça1.D9_PWM, J1.pin2
  N3: Parça1.D11_PWM/MOSI, LED1.anode
  N4: Parça1.5V, R2.leg2
  N5: Parça1.GND, R1.Pin_0, R2.leg1, R3.Pin_0
  N6: J1.pin1, R3.Pin_1
  N7: LED1.cathode, R1.Pin_1
