# Fritzing sketch cakar_devre (saved by Fritzing 0.9.3b)
breadboards: 1

parts:
  Parça1 = Arduino Uno (Rev3)
  R1 = Resistor [tolerance=±5% resistance=220 package=THT]
  R2 = Resistor [tolerance=±5% resistance=220 package=THT]
  LED1 = LED - 5mm [color="Red (633nm)" package="5 mm [THT]"]
  LED2 = LED - 5mm [color="Red (633nm)" package="5 mm [THT]"]

nets:
  N1: Parça1.D12/MISO, R1.Pin_1, LED2.cathode, LED2.anode
  N2: Parça1.D13/SCK, R2.Pin_1, LED1.cathode, LED1.anode
  N3: Parça1.GND, R1.Pin_0, R2.Pin_0
