# Fritzing sketch dc_motor (saved by Fritzing 0.9.3b)
breadboards: 1

parts:
  M1 = DC Motor
  L298N1 = L298N DC motor driver
  VCC1 = Battery
  VCC2 = Battery
  Parça1 = Arduino Uno (Rev3)

nets:
  N1: M1.pin_1, L298N1.OUT2
  N2: M1.pin_2, L298N1.OUT1
  N3: L298N1.12V, VCC2.+
  N4: L298N1.GND, VCC1.-
  N5: L298N1.ENA, Parça1.D9_PWM
  N6: L298N1.IN1, Parça1.D8
  N7: L298N1.IN2, Parça1.D7

custom parts:
  L298N DC motor driver: 2x DC motor driver with 78M05 positive voltage regulator (7..35 V) L298N: max 46 V, 2 A Set 5 V Enable jumper to enable 5 V regultor (needed for the L298N) and +5 V output at screw terminal or supply external +5 V at screw terminal Set ENA and/or ENB to +5 V to enable motor permanently or supply ENA and/or ENB with PWM signal IN1 and IN2 set rotation directory for motor A (OUT1/OUT2) IN2 and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
