# Fritzing sketch gaz_sensor (saved by Fritzing 0.9.3b)
breadboards: 1

parts:
  Mod1 = MQ-7 breakout
  LED1 = RGB LED (com. anode, rbg) [package="5 mm [THT]"]
  R1 = Resistor [tolerance=±5% resistance=220 package=THT]
  Parça1 = Arduino Uno (Rev3)
  R2 = Resistor [tolerance=±5% resistance=220 package=THT]
  R3 = Resistor [tolerance=±5% resistance=220 package=THT]

nets:
  VCC: Mod1.VCC, Parça1.5V
  GND: Mod1.GND, LED1.common_anode, Parça1.GND
  N1: Mod1.AO, Parça1.A0
  N2: LED1.red_cathode, R1.Pin_1
  N3: LED1.blue_cathode, R2.Pin_1
  N4: LED1.green_cathode, R3.Pin_1
  N5: R1.Pin_0, Parça1.D10_PWM/SS
  N6: Parça1.D8, R3.Pin_0
  N7: Parça1.D9_PWM, R2.Pin_0

custom parts:
  MQ-7 breakout: MQ-5 gas sensor
