# Fritzing sketch gunes_solar (saved by Fritzing 0.9.3b)
breadboards: 1

parts:
  D1 = SOLAR-IXYS [package=solarbit-12x1]
  Parça1 = Arduino Uno (Rev3)

nets:
  N1: D1.A, Parça1.A0
  N2: D1.C, Parça1.GND
