# Fritzing sketch ilk_devre (saved by Fritzing 0.9.3b)
breadboards: 1

parts:
  Parça1 = Arduino Uno (Rev3)
  R1 = Resistor [tolerance=±5% resistance=220 package=THT]  # not connected
  LED1 = LED - 5mm [color="Red (633nm)" package="5 mm [THT]"]
  R2 = Resistor [tolerance=±5% resistance=220 package=THT]

nets:
  N1: Parça1.D13/SCK, LED1.anode
  N2: Parça1.GND, R2.Pin_0
  N3: LED1.cathode, R2.Pin_1

// code stored in the sketch: Untitled.ino
void setup() {
  pinMode(LED_BUILTIN, OUTPUT);//13. pin
}


void loop() {
  digitalWrite(LED_BUILTIN, HIGH);  
  digitalWrite(LED_BUILTIN, HIGH); 
  digitalWrite(LED_BUILTIN, HIGH); 
  delay(1000);
  digitalWrite(LED_BUILTIN, LOW); 
  delay(1000);
}
