# Fritzing sketch lazer (saved by Fritzing 0.9.3b)
breadboards: 1

parts:
  Parça1 = Arduino Uno (Rev3)
  KY-008_Laserdiode2 = Laser [part_number=1219301 package=keys]

nets:
  N1: Parça1.D7, KY-008_Laserdiode2.connector0pin
  N2: Parça1.5V, KY-008_Laserdiode2.connector1pin
  N3: Parça1.GND, KY-008_Laserdiode2.connector2pin

custom parts:
  Laser: KEYES KY-008 650nm Laser Transmitter Module
