# Fritzing sketch lazer_hareket (saved by Fritzing 0.9.3b)
breadboards: 1

parts:
  KY-008_Laserdiode2 = Laser [part_number=1219301 package=keys]
  Parça1 = Arduino Uno (Rev3)
  J1 = Basic Servo
  J2 = Basic Servo
  Parça2 = Thumb Joystick

nets:
  N1: KY-008_Laserdiode2.connector0pin, Parça1.D3_PWM
  VCC: KY-008_Laserdiode2.connector1pin, Parça1.5V, J1.vcc, J2.vcc, Parça2.VCC
  GND: KY-008_Laserdiode2.connector2pin, Parça1.GND, J1.gnd, J2.gnd, Parça2.GND
  N2: Parça1.A0, Parça2.HORZ
  N3: Parça1.A1, Parça2.SEL
  N4: Parça1.D9_PWM, J1.pulse
  N5: Parça1.D10_PWM/SS, J2.pulse
  N6: Parça1.D4, Parça2.VERT

custom parts:
  Laser: KEYES KY-008 650nm Laser Transmitter Module
