# Fritzing sketch lcd_ekran_2 (saved by Fritzing 0.9.3b)
breadboards: 1

parts:
  LCD1 = LCD screen
  R1 = Rotary Potentiometer (Small) [maximum_resistance=100kΩ package=THT]
  R2 = Resistor [tolerance=±5% resistance=220 package=THT]
  Parça1 = Arduino Uno (Rev3)

nets:
  VSS: LCD1.VSS, LCD1.R/W, LCD1.LED-, R1.leg1, Parça1.GND
  VDD: LCD1.VDD, R1.leg2, R2.Pin_1, Parça1.5V
  N1: LCD1.V0, R1.wiper
  N2: LCD1.RS, Parça1.D12/MISO
  N3: LCD1.DB0, Parça1.D11_PWM/MOSI
  N4: LCD1.DB4, Parça1.D5_PWM
  N5: LCD1.DB5, Parça1.D4
  N6: LCD1.DB6, Parça1.D3_PWM
  N7: LCD1.DB7, Parça1.D2
  N8: LCD1.LED+, R2.Pin_0
