# Fritzing sketch ldr_lazer (saved by Fritzing 0.9.3b)
breadboards: 1

parts:
  Parça2 = Arduino Uno (Rev3)
  KY-008_Laserdiode3 = Laser [part_number=1219301 package=keys]
  R1 = Resistor [tolerance=±5% resistance=220 package=THT]
  R2 = Photocell (LDR) [package=THT]

nets:
  N1: Parça2.A0, R1.Pin_1, R2.pin_0
  N2: Parça2.D7, KY-008_Laserdiode3.connector0pin
  N3: Parça2.5V, KY-008_Laserdiode3.connector1pin, R2.pin_1
  N4: Parça2.GND, KY-008_Laserdiode3.connector2pin, R1.Pin_0

custom parts:
  Laser: KEYES KY-008 650nm Laser Transmitter Module
