# Fritzing sketch ldr_sensor (saved by Fritzing 0.9.3b)
breadboards: 1

parts:
  R1 = Photocell (LDR) [package=THT]
  Parça1 = Arduino Uno (Rev3)
  R2 = Resistor [tolerance=±5% resistance=220 package=THT]

nets:
  N1: R1.pin_0, Parça1.A0, R2.Pin_1
  N2: R1.pin_1, Parça1.5V
  N3: Parça1.GND, R2.Pin_0
