# Fritzing sketch lm-35-isi-olcme (saved by Fritzing 0.9.3b)
breadboards: 1

parts:
  T1 = LM35 Temperature Sensor [package="TO92 [THT]"]
  Parça1 = Arduino Uno (Rev3)

nets:
  N1: T1.+Vs, Parça1.5V
  N2: T1.Vout, Parça1.A0
  GND: T1.GND, Parça1.GND
