# Fritzing sketch mesafe_sensor (saved by Fritzing 0.9.3b)
breadboards: 1

parts:
  Parça1 = Arduino Uno (Rev3)
  hc-sr1 = hc-sr04

nets:
  N1: Parça1.D5_PWM, hc-sr1.Trig
  N2: Parça1.D6_PWM, hc-sr1.Echo
  5V: Parça1.5V, hc-sr1.VCC
  GND: Parça1.GND, hc-sr1.GND
