# Fritzing sketch mini_reed (saved by Fritzing 0.9.3b)
breadboards: 1

parts:
  S1 = SWITCH-MOMENTARY-2 [package=reed_switch_plastic]
  Parça1 = Arduino Uno (Rev3)
  R1 = Resistor [tolerance=±5% resistance=10 package=THT]

nets:
  N1: S1.1, Parça1.GND, R1.Pin_0
  N2: S1.2, Parça1.D7, R1.Pin_1
