# Fritzing sketch pir_sensor (saved by Fritzing 0.9.3b)
breadboards: 1

parts:
  Parça1 = Arduino Uno (Rev3)
  Parça2 = HC-SR501 Body Sensor Module

nets:
  N1: Parça1.D9_PWM, Parça2.OUT
  GND: Parça1.GND, Parça2.GND
  5V: Parça1.5V, Parça2.VCC

custom parts:
  HC-SR501 Body Sensor Module: Pyroelectric Infrared PIR Motion Sensor Detector Module
