# Fritzing sketch rgb_led (saved by Fritzing 0.9.3b)
breadboards: 1

parts:
  Parça1 = Arduino Uno (Rev3)
  LED1 = RGB LED (com. cathode, rgb) [package="5 mm [THT]"]
  R1 = Resistor [tolerance=±5% resistance=220 package=THT]
  R2 = Resistor [tolerance=±5% resistance=220 package=THT]
  R3 = Resistor [tolerance=±5% resistance=220 package=THT]
  LED2 = RGB LED (com. cathode, rgb) [package="5 mm [THT]"]  # not connected

nets:
  N1: Parça1.D9_PWM, R1.Pin_1
  N2: Parça1.D10_PWM/SS, R2.Pin_1
  N3: Parça1.D11_PWM/MOSI, R3.Pin_1
  N4: Parça1.GND, LED1.common_cathode
  N5: LED1.red_anode, R1.Pin_0
  N6: LED1.green_anode, R2.Pin_0
  N7: LED1.blue_anode, R3.Pin_0
