# Fritzing sketch ses_sensor (saved by Fritzing 0.9.3b)
breadboards: 1

parts:
  Parça1 = Breakout Board for Electret Microphone
  Parça2 = Arduino Uno (Rev3)
  KY-008_Laserdiode2 = Laser [part_number=1219301 package=keys]  # not connected
  LED1 = LED - 5mm [color="Red (633nm)" package="5 mm [THT]"]

nets:
  VCC: Parça1.VCC, Parça2.5V
  GND: Parça1.GND, Parça2.GND, LED1.cathode
  N1: Parça1.AUD, Parça2.D8
  N2: Parça2.D9_PWM, LED1.anode

custom parts:
  Laser: KEYES KY-008 650nm Laser Transmitter Module
