# Fritzing sketch trafik_isigi (saved by Fritzing 0.9.3b)
breadboards: 1

parts:
  LED1 = LED - 5mm [color="Red (633nm)" package="5 mm [THT]"]
  LED2 = LED - 5mm [color="Yellow (595nm)" package="5 mm [THT]"]
  LED3 = LED - 5mm [color="Green (570nm)" package="5 mm [THT]"]
  R1 = Resistor [tolerance=±5% resistance=220 package=THT]
  R2 = Resistor [tolerance=±5% resistance=220 package=THT]
  R3 = Resistor [tolerance=±5% resistance=220 package=THT]
  Parça1 = Arduino Uno (Rev3)
  LED4 = LED - 5mm [color="Red (633nm)" package="5 mm [THT]"]
  LED6 = LED - 5mm [color="Green (570nm)" package="5 mm [THT]"]
  R4 = Resistor [tolerance=±5% resistance=220 package=THT]
  R6 = Resistor [tolerance=±5% resistance=220 package=THT]

nets:
  N1: LED1.cathode, Parça1.D13/SCK
  N2: LED1.anode, R1.Pin_1
  N3: LED2.cathode, Parça1.D12/MISO
  N4: LED2.anode, R2.Pin_1
  N5: LED3.cathode, Parça1.D11_PWM/MOSI
  N6: LED3.anode, R3.Pin_1
  N7: R1.Pin_0, R2.Pin_0, R3.Pin_0, Parça1.GND, R4.Pin_0, R6.Pin_0
  N8: Parça1.D9_PWM, LED6.cathode
  N9: Parça1.D10_PWM/SS, LED4.cathode
  N10: LED4.anode, R4.Pin_1
  N11: LED6.anode, R6.Pin_1
